// Logisim project sequential-counter.circ as structural Verilog: 1 circuit, main circuit main
module main (
);

  wire and_1_out, clock_1_out, nand_1_out, not_1_out;
  wire [2:0] j_k_ff_2_q;
  wire [3:0] j_k_ff_1_q;

  Clock clock_1 (.out(clock_1_out));
  J_K_Flip_Flop #(.trigger("falling")) j_k_ff_1 (
    .J(1'b1), .clk(clock_1_out), .K(1'b1), .Q(j_k_ff_1_q[0]), .reset(not_1_out));  // open: Qn, preset, en
  not not_1 (not_1_out, nand_1_out);
  J_K_Flip_Flop #(.trigger("falling")) j_k_ff_2 (
    .J(1'b1), .clk(nand_1_out), .K(1'b1), .Q(j_k_ff_2_q[0]), .reset(and_1_out));  // open: Qn, preset, en
  J_K_Flip_Flop #(.trigger("falling")) j_k_ff_3 (
    .J(1'b1), .clk(j_k_ff_1_q[0]), .K(1'b1), .Q(j_k_ff_1_q[1]), .reset(not_1_out));  // open: Qn, preset, en
  J_K_Flip_Flop #(.trigger("falling")) j_k_ff_4 (
    .J(1'b1), .clk(j_k_ff_2_q[0]), .K(1'b1), .Q(j_k_ff_2_q[1]), .reset(and_1_out));  // open: Qn, preset, en
  nand nand_1 (nand_1_out, j_k_ff_1_q[1], j_k_ff_1_q[3]);
  and and_1 (and_1_out, j_k_ff_2_q[1], j_k_ff_2_q[2]);
  J_K_Flip_Flop #(.trigger("falling")) j_k_ff_5 (
    .J(1'b1), .clk(j_k_ff_1_q[1]), .K(1'b1), .Q(j_k_ff_1_q[2]), .reset(not_1_out));  // open: Qn, preset, en
  J_K_Flip_Flop #(.trigger("falling")) j_k_ff_6 (
    .J(1'b1), .clk(j_k_ff_2_q[1]), .K(1'b1), .Q(j_k_ff_2_q[2]), .reset(and_1_out));  // open: Qn, preset, en
  J_K_Flip_Flop #(.trigger("falling")) j_k_ff_7 (
    .J(1'b1), .clk(j_k_ff_1_q[2]), .K(1'b1), .Q(j_k_ff_1_q[3]), .reset(not_1_out));  // open: Qn, preset, en
  // Probe on j_k_ff_1_q
  // Probe on j_k_ff_2_q
endmodule
